// Digital circuit bubble_loaded_3.dig as structural Verilog
module bubble_loaded_3 (
  input  [8:0] N,
  input  reset,
  input  start,
  input  clock,
  output done,
  output [7:0] displayout,
  output [15:0] clockcount,
  output valid
);

  wire _1_lt__r, _2_lt__t, and_1_out, and_2_out, and_3_out, and_4_out, and_5_out, and_6_out, done_t, eq_N,
       i_eq_N, i_eq_n_t, i_gt_n, idle, inc, inc_i, inc_j, j_eq_n_i, ld, multiplexer_1_out, multiplexer_2_out,
       multiplexer_5_out, multiplexer_6_out, multiplexer_7_out, multiplexer_8_out, not_1_out, not_2_out,
       not_3_out, not_4_out, not_5_out, or_1_out, or_2_out, port_done, r_lt__2, rs_ff_as_1_q, sort_idle, str,
       str_temp, t_gt_r, t_lt__1, trans, up, xor_1_out;
  wire [1:0] d_ff_1_q;
  wire [3:0] d_ff_3_q;
  wire [7:0] D, Din, r_q, t_q, temp;
  wire [8:0] A, A_RAM, A_ROM, add_1_s, counter_2_out, i_out, j_out, multiplexer_9_out, N_t, sub_2_s;

  Multiplexer #(.Selector_Bits(2)) multiplexer_1 (
    .sel(d_ff_1_q), .in_0(start), .in_1(i_eq_N), .in_2(1'b1), .in_3(1'b1), .out(multiplexer_1_out));
  Multiplexer #(.Selector_Bits(2)) multiplexer_2 (
    .sel(d_ff_1_q), .in_0(1'b0), .in_1(1'b1), .in_2(1'b0), .in_3(1'b1), .out(multiplexer_2_out));
  Counter #(.Bits(9)) c (.en(inc), .C(clock), .clr(idle), .out(A_ROM));  // open: ovf
  and and_1 (and_1_out, ~reset, multiplexer_1_out);  // And
  and and_2 (and_2_out, ~reset, multiplexer_2_out);  // And
  Comparator #(.Bits(9)) comparator_1 (.a(N_t), .b(A_ROM), .eq(i_eq_N));  // open: gt, lt
  D_FF d_ff_1 (.D(and_1_out), .C(clock), .Q(d_ff_1_q[0]));  // open: nQ
  D_FF d_ff_2 (.D(and_2_out), .C(clock), .Q(d_ff_1_q[1]));  // open: nQ
  Decoder #(.Selector_Bits(2)) decoder_1 (.sel(d_ff_1_q), .out_0(idle), .out_1(trans), .out_2(inc), .out_3(port_done));
  Sub #(.Bits(9)) sub_1 (.a(N), .b(9'h1), .c_i(1'b0), .s(N_t));  // open: c_o
  ROM #(.AddrBits(9), .Bits(8)) ROMFILE (.A(A_ROM), .sel(trans), .D(D));
  Multiplexer multiplexer_3 (.sel(port_done), .in_0(trans), .in_1(str_temp), .out(str));
  not not_1 (not_1_out, j_eq_n_i);
  not not_2 (not_2_out, i_gt_n);
  not not_3 (not_3_out, j_eq_n_i);
  not not_4 (not_4_out, i_gt_n);
  not not_5 (not_5_out, i_eq_n_t);
  Multiplexer #(.Bits(8)) multiplexer_4 (.sel(port_done), .in_0(D), .in_1(temp), .out(Din));
  Multiplexer #(.Selector_Bits(4)) multiplexer_5 (
    .sel(d_ff_3_q), .in_0(port_done), .in_1(t_gt_r), .in_2(1'b1), .in_3(not_1_out), .in_4(1'b1),
    .in_5(not_2_out), .in_6(1'b1), .in_7(1'b0), .in_8(1'b0), .in_9(1'b0), .in_10(1'b1), .in_11(1'b0),
    .in_12(1'b0), .in_13(eq_N), .in_14(1'b1), .in_15(1'b1), .out(multiplexer_5_out));
  Multiplexer #(.Selector_Bits(4)) multiplexer_6 (
    .sel(d_ff_3_q), .in_0(1'b0), .in_1(1'b1), .in_2(1'b1), .in_3(1'b0), .in_4(1'b0), .in_5(i_gt_n),
    .in_6(1'b0), .in_7(1'b0), .in_8(1'b0), .in_9(1'b1), .in_10(1'b0), .in_11(1'b0), .in_12(1'b1),
    .in_13(1'b1), .in_14(1'b0), .in_15(1'b1), .out(multiplexer_6_out));
  Multiplexer #(.Selector_Bits(4)) multiplexer_7 (
    .sel(d_ff_3_q), .in_0(1'b0), .in_1(1'b0), .in_2(1'b0), .in_3(j_eq_n_i), .in_4(1'b1), .in_5(i_gt_n),
    .in_6(1'b1), .in_7(1'b0), .in_8(1'b0), .in_9(i_eq_n_t), .in_10(1'b0), .in_11(1'b1), .in_12(1'b0),
    .in_13(1'b1), .in_14(1'b1), .in_15(1'b1), .out(multiplexer_7_out));
  Multiplexer #(.Selector_Bits(4)) multiplexer_8 (
    .sel(d_ff_3_q), .in_0(port_done), .in_1(t_gt_r), .in_2(1'b0), .in_3(not_3_out), .in_4(1'b0),
    .in_5(not_4_out), .in_6(1'b1), .in_7(1'b0), .in_8(1'b0), .in_9(not_5_out), .in_10(1'b0), .in_11(1'b1),
    .in_12(1'b0), .in_13(1'b1), .in_14(1'b1), .in_15(1'b1), .out(multiplexer_8_out));
  RAMDualPort #(.AddrBits(9), .Bits(8)) RAM (.A(A), .Din(Din), .str(str), .C(clock), .ld(ld), .D(displayout));
  Multiplexer #(.Bits(9)) multiplexer_9 (.sel(port_done), .in_0(A_ROM), .in_1(A_RAM), .out(multiplexer_9_out));
  and and_3 (and_3_out, ~reset, multiplexer_5_out);  // And
  and and_4 (and_4_out, ~reset, multiplexer_6_out);  // And
  and and_5 (and_5_out, ~reset, multiplexer_7_out);  // And
  and and_6 (and_6_out, ~reset, multiplexer_8_out);  // And
  D_FF d_ff_3 (.D(and_3_out), .C(clock), .Q(d_ff_3_q[0]));  // open: nQ
  D_FF d_ff_4 (.D(and_4_out), .C(clock), .Q(d_ff_3_q[1]));  // open: nQ
  D_FF d_ff_5 (.D(and_5_out), .C(clock), .Q(d_ff_3_q[2]));  // open: nQ
  D_FF d_ff_6 (.D(and_6_out), .C(clock), .Q(d_ff_3_q[3]));  // open: nQ
  Seven_Seg_Hex seven_seg_hex_1 (.d(displayout[7:4]), .dp(1'b0));
  Seven_Seg_Hex seven_seg_hex_2 (.d(displayout[3:0]), .dp(1'b0));
  xor xor_1 (xor_1_out, done, start);
  RS_FF_AS rs_ff_as_1 (.S(done_t), .R(reset), .Q(rs_ff_as_1_q));  // open: nQ
  Decoder #(.Selector_Bits(4)) decoder_2 (
    .sel(d_ff_3_q), .out_0(sort_idle), .out_2(inc_j), .out_4(inc_i), .out_6(done_t), .out_9(t_lt__1),
    .out_10(r_lt__2), .out_11(_2_lt__t), .out_12(_1_lt__r), .out_13(valid), .out_14(up), .out_15(done));  // open: out_1, out_3, out_5, out_7, out_8
  Multiplexer #(.Bits(9)) multiplexer_10 (.sel(rs_ff_as_1_q), .in_0(multiplexer_9_out), .in_1(counter_2_out), .out(A));
  Counter #(.Bits(16)) counter_1 (.en(xor_1_out), .C(clock), .clr(reset), .out(clockcount));  // open: ovf
  Counter #(.Bits(9)) j (.en(inc_j), .C(clock), .clr(inc_i), .out(j_out));  // open: ovf
  Counter #(.Bits(9)) i (.en(inc_i), .C(clock), .clr(sort_idle), .out(i_out));  // open: ovf
  Counter #(.Bits(9)) counter_2 (.en(up), .C(clock), .clr(reset), .out(counter_2_out));  // open: ovf
  Register #(.Bits(8)) t (.D(displayout), .C(clock), .en(t_lt__1), .Q(t_q));
  Register #(.Bits(8)) r (.D(displayout), .C(clock), .en(r_lt__2), .Q(r_q));
  Add #(.Bits(9)) add_1 (.a(j_out), .b({9{1'b0}}), .c_i(1'b1), .s(add_1_s));  // open: c_o
  Sub #(.Bits(9)) sub_2 (.a(N_t), .b(i_out), .c_i(1'b0), .s(sub_2_s));  // open: c_o
  Comparator #(.Bits(9)) comparator_2 (.a(counter_2_out), .b(N_t), .eq(eq_N));  // open: gt, lt
  Comparator #(.Bits(8)) comparator_3 (.a(t_q), .b(r_q), .gt(t_gt_r));  // open: eq, lt
  Multiplexer #(.Bits(8)) multiplexer_11 (.sel(or_1_out), .in_0(t_q), .in_1(r_q), .out(temp));
  or or_1 (or_1_out, r_lt__2, _1_lt__r);
  Multiplexer #(.Bits(9)) multiplexer_12 (.sel(or_2_out), .in_0(j_out), .in_1(add_1_s), .out(A_RAM));
  or or_2 (or_2_out, r_lt__2, _2_lt__t);
  Comparator #(.Bits(9)) comparator_4 (.a(j_out), .b(sub_2_s), .eq(j_eq_n_i));  // open: gt, lt
  Comparator #(.Bits(9)) comparator_5 (.a(i_out), .b(N_t), .gt(i_gt_n), .eq(i_eq_n_t));  // open: lt
  or or_3 (str_temp, _2_lt__t, _1_lt__r);
  or or_4 (ld, t_lt__1, valid, r_lt__2);

  // Other names for the same wires on the sheet: display = valid; done_for_real = done; Dout[7:0] = displayout;
  //   port_start = start

  // Notes on the sheet:
  //   clock: Hz: 5
  //   ROM-to-RAM-porting
  //   control path
  //   data path
  //   RAM-sorting
  //   contents of ROMFILE (hex, n*v repeats v):
  //   a,28,14,1e,f
endmodule
