// Digital circuit prototype_project.dig as structural Verilog
module prototype_project (
  input  start,
  input  clk,
  input  [8:0] N,
  output Done
);

  wire a, and_3_out, and_4_out, and_5_out, and_6_out, and_7_out, and_8_out, clk_t, comparator_1_eq,
       comparator_2_eq, fin, ind, S;
  wire [7:0] counter_2_out, data, num, ramdualport_1_d;
  wire [9:0] add_1_s, add_2_s, counter_1_out, counter_3_out, counter_4_out, multiplexer_1_out, n_t;

  and and_1 (S, start, ~fin);  // And
  Sub #(.Bits(10)) sub_1 (.a({1'b0, N}), .b(10'h1), .c_i(1'b0), .s(n_t));  // open: c_o
  and and_2 (clk_t, clk, start);
  and and_3 (and_3_out, a, ~fin);  // And
  Comparator #(.Bits(10)) comparator_1 (.a(counter_1_out), .b(n_t), .eq(comparator_1_eq));  // open: gt, lt
  Comparator #(.Bits(8)) comparator_2 (.a(counter_2_out), .b({8{1'b1}}), .eq(comparator_2_eq));  // open: gt, lt
  Comparator #(.Bits(10)) comparator_3 (.a(counter_1_out), .b(10'h1), .eq(a));  // open: gt, lt
  Counter #(.Bits(10)) counter_1 (.en(S), .C(clk_t), .clr(comparator_1_eq), .out(counter_1_out));  // open: ovf
  Counter #(.Bits(8)) counter_2 (.en(S), .C(and_3_out), .clr(comparator_2_eq), .out(counter_2_out));  // open: ovf
  Demultiplexer #(.Bits(8)) demultiplexer_1 (.sel(ind), .in(data), .out_1(num));  // open: out_0
  ROM #(.AddrBits(10), .Bits(8)) rom_1 (.A(counter_1_out), .sel(start), .D(data));
  Comparator #(.Bits(8)) comparator_4 (.a(counter_2_out), .b(data), .eq(ind));  // open: gt, lt
  Add #(.Bits(10)) add_1 (.a({1'b0, N}), .b(10'h1), .c_i(1'b0), .s(add_1_s));  // open: c_o
  and and_4 (and_4_out, clk_t, ~Done);  // And
  and and_5 (and_5_out, fin, ~Done);  // And
  and and_6 (and_6_out, ind, ~fin);  // And
  Comparator #(.Bits(10)) comparator_5 (.a(counter_3_out), .b(add_1_s), .eq(fin));  // open: gt, lt
  Counter #(.Bits(10)) counter_3 (.en(~fin), .C(and_6_out), .clr(fin), .out(counter_3_out));  // open: ovf
  and and_7 (and_7_out, ~fin, ind);  // And
  Comparator #(.Bits(10)) comparator_6 (.a(counter_4_out), .b({1'b0, N}), .eq(Done));  // open: gt, lt
  Counter #(.Bits(10)) counter_4 (.en(and_5_out), .C(and_4_out), .clr(Done), .out(counter_4_out));  // open: ovf
  Add #(.Bits(10)) add_2 (.a(counter_4_out), .b(10'h1), .c_i(1'b0), .s(add_2_s));  // open: c_o
  Multiplexer #(.Bits(10)) multiplexer_1 (.sel(fin), .in_0(counter_3_out), .in_1(add_2_s), .out(multiplexer_1_out));
  RAMDualPort #(.AddrBits(10), .Bits(8)) ramdualport_1 (
    .A(multiplexer_1_out), .Din(num), .str(and_7_out), .C(clk_t), .ld(and_8_out), .D(ramdualport_1_d));
  and and_8 (and_8_out, fin, ~Done);  // And
  Seven_Seg_Hex seven_seg_hex_1 (.d(ramdualport_1_d[7:4]), .dp(1'b0));
  Seven_Seg_Hex seven_seg_hex_2 (.d(ramdualport_1_d[3:0]), .dp(1'b0));

  // Other names for the same wires on the sheet: nl[8:0] = N; S0 = start

  // Notes on the sheet:
  //   clk: Hz: 4
  //   contents of rom_1 (hex, n*v repeats v):
  //   0,1,2,1,5,4,8,7
endmodule
