// Digital circuit tempPro3.dig as structural Verilog
module tempPro3 (
  input  [8:0] N,
  input  reset,
  input  start,
  input  clock,
  input  clock2,
  output done,
  output [7:0] displayout,
  output valid,
  output [15:0] clockcount
);

  wire and_1_out, and_2_out, and_3_out, and_4_out, and_5_out, and_6_out, and_7_out, comparator_1_eq,
       comparator_2_gt, comparator_3_eq, comparator_4_eq, decoder_1_out_0, decoder_1_out_2, decoder_1_out_5,
       decoder_2_out_0, decoder_2_out_2, decoder_2_out_4, decoder_2_out_9, decoder_2_out_10,
       decoder_2_out_11, decoder_2_out_12, done2, multiplexer_1_out, multiplexer_2_out, multiplexer_3_out,
       multiplexer_4_out, multiplexer_5_out, multiplexer_6_out, multiplexer_7_out, multiplexer_12_out,
       multiplexer_15_out, not_1_out, not_2_out, not_3_out, not_4_out, not_5_out, or_1_out, or_2_out,
       or_3_out, or_4_out, relay_2_p1, str, xor_1_out, xor_2_out;
  wire [2:0] d_ff_1_q;
  wire [3:0] d_ff_4_q;
  wire [7:0] Din, multiplexer_8_out, multiplexer_11_out, r_q, RAM_d, t_q;
  wire [8:0] A, add_1_s, i_2_out, j_out, multiplexer_9_out, multiplexer_14_out, multiplexer_16_out, N_1,
       relay_1_p4, sub_1_s, sub_2_s;
  wire [15:0] clockcount_t, clockcounta, clockcountb;

  not not_1 (not_1_out, comparator_1_eq);
  Multiplexer #(.Selector_Bits(3)) multiplexer_1 (
    .sel(d_ff_1_q), .in_0(start), .in_1(1'b1), .in_2(1'b1), .in_3(1'b0), .in_4(1'b0), .in_5(1'b1),
    .in_6(1'b0), .in_7(1'b0), .out(multiplexer_1_out));
  Multiplexer #(.Selector_Bits(3)) multiplexer_2 (
    .sel(d_ff_1_q), .in_0(1'b0), .in_1(not_1_out), .in_2(1'b0), .in_3(1'b1), .in_4(1'b0), .in_5(1'b0),
    .in_6(1'b0), .in_7(1'b0), .out(multiplexer_2_out));
  Multiplexer #(.Selector_Bits(3)) multiplexer_3 (
    .sel(d_ff_1_q), .in_0(1'b0), .in_1(comparator_1_eq), .in_2(1'b0), .in_3(1'b0), .in_4(1'b0), .in_5(1'b1),
    .in_6(1'b0), .in_7(1'b0), .out(multiplexer_3_out));
  Counter #(.Bits(9)) i (.en(decoder_1_out_2), .C(clock), .clr(decoder_1_out_0), .out(A));  // open: ovf
  and and_1 (and_1_out, ~reset, multiplexer_1_out);  // And
  and and_2 (and_2_out, ~reset, multiplexer_2_out);  // And
  and and_3 (and_3_out, ~reset, multiplexer_3_out);  // And
  Comparator #(.Bits(9)) comparator_1 (.a(N), .b(A), .eq(comparator_1_eq));  // open: gt, lt
  ROM #(.AddrBits(9), .Bits(8)) ROMFILE (.A(A), .sel(str), .D(Din));
  D_FF d_ff_1 (.D(and_1_out), .C(clock), .Q(d_ff_1_q[0]));  // open: nQ
  D_FF d_ff_2 (.D(and_2_out), .C(clock), .Q(d_ff_1_q[1]));  // open: nQ
  D_FF d_ff_3 (.D(and_3_out), .C(clock), .Q(d_ff_1_q[2]));  // open: nQ
  Decoder #(.Selector_Bits(3)) decoder_1 (
    .sel(d_ff_1_q), .out_0(decoder_1_out_0), .out_2(decoder_1_out_2), .out_3(str), .out_5(decoder_1_out_5));  // open: out_1, out_4, out_6, out_7
  Sub #(.Bits(9)) sub_1 (.a(N), .b({9{1'b0}}), .c_i(1'b1), .s(sub_1_s));  // open: c_o
  not not_2 (not_2_out, comparator_3_eq);
  not not_3 (not_3_out, comparator_4_eq);
  not not_4 (not_4_out, comparator_3_eq);
  not not_5 (not_5_out, comparator_4_eq);
  Multiplexer #(.Selector_Bits(4)) multiplexer_4 (
    .sel(d_ff_4_q), .in_0(decoder_1_out_5), .in_1(comparator_2_gt), .in_2(1'b1), .in_3(not_2_out),
    .in_4(1'b1), .in_5(not_3_out), .in_6(1'b0), .in_7(1'b0), .in_8(1'b0), .in_9(1'b0), .in_10(1'b1),
    .in_11(1'b0), .in_12(1'b0), .in_13(1'b0), .in_14(1'b0), .in_15(1'b0), .out(multiplexer_4_out));
  Multiplexer #(.Selector_Bits(4)) multiplexer_5 (
    .sel(d_ff_4_q), .in_0(1'b0), .in_1(1'b1), .in_2(1'b1), .in_3(1'b0), .in_4(1'b0), .in_5(comparator_4_eq),
    .in_6(1'b1), .in_7(1'b0), .in_8(1'b0), .in_9(1'b1), .in_10(1'b0), .in_11(1'b0), .in_12(1'b1),
    .in_13(1'b0), .in_14(1'b0), .in_15(1'b0), .out(multiplexer_5_out));
  Multiplexer #(.Selector_Bits(4)) multiplexer_6 (
    .sel(d_ff_4_q), .in_0(1'b0), .in_1(1'b0), .in_2(1'b0), .in_3(comparator_3_eq), .in_4(1'b1),
    .in_5(comparator_4_eq), .in_6(1'b1), .in_7(1'b0), .in_8(1'b0), .in_9(1'b0), .in_10(1'b0), .in_11(1'b1),
    .in_12(1'b0), .in_13(1'b0), .in_14(1'b0), .in_15(1'b0), .out(multiplexer_6_out));
  Multiplexer #(.Selector_Bits(4)) multiplexer_7 (
    .sel(d_ff_4_q), .in_0(decoder_1_out_5), .in_1(comparator_2_gt), .in_2(1'b0), .in_3(not_4_out),
    .in_4(1'b0), .in_5(not_5_out), .in_6(1'b0), .in_7(1'b0), .in_8(1'b0), .in_9(1'b1), .in_10(1'b0),
    .in_11(1'b1), .in_12(1'b0), .in_13(1'b0), .in_14(1'b0), .in_15(1'b0), .out(multiplexer_7_out));
  Register #(.Bits(8)) t (.D(RAM_d), .C(clock), .en(decoder_2_out_9), .Q(t_q));
  Register #(.Bits(8)) r (.D(RAM_d), .C(clock), .en(decoder_2_out_10), .Q(r_q));
  Counter #(.Bits(9)) j (.en(decoder_2_out_2), .C(clock), .clr(decoder_2_out_4), .out(j_out));  // open: ovf
  Counter #(.Bits(9)) i_2 (.en(decoder_2_out_4), .C(clock), .clr(decoder_2_out_0), .out(i_2_out));  // open: ovf
  Add #(.Bits(9)) add_1 (.a(j_out), .b({9{1'b0}}), .c_i(1'b1), .s(add_1_s));  // open: c_o
  or or_1 (or_1_out, decoder_2_out_10, decoder_2_out_12);
  and and_4 (and_4_out, ~reset, multiplexer_4_out);  // And
  and and_5 (and_5_out, ~reset, multiplexer_5_out);  // And
  and and_6 (and_6_out, ~reset, multiplexer_6_out);  // And
  and and_7 (and_7_out, ~reset, multiplexer_7_out);  // And
  Multiplexer #(.Bits(8)) multiplexer_8 (.sel(or_1_out), .in_0(t_q), .in_1(r_q), .out(multiplexer_8_out));
  Multiplexer #(.Bits(9)) multiplexer_9 (.sel(or_2_out), .in_0(j_out), .in_1(add_1_s), .out(multiplexer_9_out));
  or or_2 (or_2_out, decoder_2_out_10, decoder_2_out_11);
  D_FF d_ff_4 (.D(and_4_out), .C(clock), .Q(d_ff_4_q[0]));  // open: nQ
  D_FF d_ff_5 (.D(and_5_out), .C(clock), .Q(d_ff_4_q[1]));  // open: nQ
  D_FF d_ff_6 (.D(and_6_out), .C(clock), .Q(d_ff_4_q[2]));  // open: nQ
  D_FF d_ff_7 (.D(and_7_out), .C(clock), .Q(d_ff_4_q[3]));  // open: nQ
  Multiplexer #(.Bits(8)) multiplexer_10 (.sel(valid), .in_0({8{1'b0}}), .in_1(RAM_d), .out(displayout));
  or or_3 (or_3_out, decoder_2_out_11, decoder_2_out_12);
  Sub #(.Bits(9)) sub_2 (.a(sub_1_s), .b(i_2_out), .c_i(1'b0), .s(sub_2_s));  // open: c_o
  or or_4 (or_4_out, decoder_2_out_9, decoder_2_out_10);
  Decoder #(.Selector_Bits(4)) decoder_2 (
    .sel(d_ff_4_q), .out_0(decoder_2_out_0), .out_2(decoder_2_out_2), .out_4(decoder_2_out_4), .out_6(valid),
    .out_9(decoder_2_out_9), .out_10(decoder_2_out_10), .out_11(decoder_2_out_11), .out_12(decoder_2_out_12));  // open: out_1, out_3, out_5, out_7, out_8, out_13, out_14, out_15
  Seven_Seg_Hex seven_seg_hex_1 (.d(displayout[7:4]), .dp(1'b0));
  Comparator #(.Bits(8)) comparator_2 (.a(t_q), .b(r_q), .gt(comparator_2_gt));  // open: eq, lt
  Comparator #(.Bits(9)) comparator_3 (.a(j_out), .b(sub_2_s), .eq(comparator_3_eq));  // open: gt, lt
  Comparator #(.Bits(9)) comparator_4 (.a(i_2_out), .b(sub_1_s), .eq(comparator_4_eq));  // open: gt, lt
  Seven_Seg_Hex seven_seg_hex_2 (.d(displayout[3:0]), .dp(1'b0));
  Multiplexer #(.Bits(8)) multiplexer_11 (
    .sel(decoder_1_out_5), .in_0(Din), .in_1(multiplexer_8_out), .out(multiplexer_11_out));
  Multiplexer multiplexer_12 (.sel(decoder_1_out_5), .in_0(str), .in_1(or_3_out), .out(multiplexer_12_out));
  // Relay relay_1: pin names not known; wires that end beside it: or_4_out, valid, 1'b1, relay_1_p4
  // Relay #(.relayNormallyClosed("true")) relay_2: pin names not known; wires that end beside it: relay_2_p1, valid, 1'b1, valid
  Multiplexer #(.Bits(16)) multiplexer_13 (.sel(reset), .in_0(clockcount_t), .in_1({16{1'b0}}), .out(clockcount));
  Multiplexer #(.Bits(9)) multiplexer_14 (
    .sel(decoder_1_out_5), .in_0(A), .in_1(multiplexer_9_out), .out(multiplexer_14_out));
  Multiplexer multiplexer_15 (.sel(done2), .in_0(valid), .in_1(1'b0), .out(multiplexer_15_out));
  RAMDualPort #(.AddrBits(9), .Bits(8)) RAM (
    .A(multiplexer_16_out), .Din(multiplexer_11_out), .str(multiplexer_12_out), .C(clock), .ld(relay_2_p1),
    .D(RAM_d));
  Counter #(.Bits(9)) j_2 (.en(multiplexer_15_out), .C(clock2), .clr(reset), .out(relay_1_p4));  // open: ovf
  Multiplexer #(.Bits(9)) multiplexer_16 (
    .sel(valid), .in_0(multiplexer_14_out), .in_1(relay_1_p4), .out(multiplexer_16_out));
  xor xor_1 (xor_1_out, done, valid);
  and and_8 (done, valid, done2);
  Comparator #(.Bits(9)) comparator_5 (.a(N_1), .b(relay_1_p4), .eq(done2));  // open: gt, lt
  Sub #(.Bits(9)) sub_3 (.a(N), .b(9'h1), .c_i(1'b0), .s(N_1));  // open: c_o
  Counter #(.Bits(16)) counter_1 (.en(xor_1_out), .C(clock2), .clr(reset), .out(clockcountb));  // open: ovf
  xor xor_2 (xor_2_out, valid, start);
  Add #(.Bits(16)) add_2 (.a(clockcounta), .b(clockcountb), .c_i(1'b0), .s(clockcount_t));  // open: c_o
  Counter #(.Bits(16)) counter_2 (.en(xor_2_out), .C(clock), .clr(reset), .out(clockcounta));  // open: ovf

  // Other names for the same wires on the sheet: done_t = valid; rdone = done

  // Notes on the sheet:
  //   clock: Hz: 5000
  //   contents of ROMFILE (hex, n*v repeats v):
  //   3f,c2,7f,d6,6e,1e,db,53,49,9e,83,c3,57,10,f9,22,e0,f7,fd,17,b2
  //   ,d9,b6,9b,c4,7,d1,77,1b,ed,30,e,36,12,17,7a,ed,8,fc,2a,a9,8b,ad
  //   ,66,2e,fd,7a,41,c9,45,65,52,fa,bd,91,a4,7,94,d6,6d,f7,2a,62,8c
  //   ,63,a4,f0,e7,13,f6,14,41,ff,f6,75,e,1f,18,d,a3,4a,d7,a1,1d,cc
  //   ,27,7c,5f,2,80,31,b7,ff,de,f8,19,c4,6a,62,c5,f7,ba,ae,a,99,3c
  //   ,d9,2d,f9,15,db,8b,28,d1,5b,d0,48,2f,c,32,9f,86,8d,a2,73,47,62
  //   ,9b,e8,ee,1e,2,d1,14,49,50,34,3b,bb,31,8b,16,a4,6a,e7,9c,89,c2
  //   ,a2,4e,d4,b8,9a,d0,a1,6f,96,de,83,c8,c3,bc,4b,e1,6f,df,3d,5e,19
  //   ,3a,a0,1b,62,eb,aa,e6,43,12,44,d7,e,2d,5d,4,34,97,57,ea,ef,e,ec
  //   ,95,ac,d1,a0,e0,d4,bd,d7,11,b4,21,aa,eb,96,dc,ed,56,e3,c4,c5,4d
  //   ,40,cc,0,79,88,4e,ea,f2,90,63,2a,2d,a7,c3,c5,5c,2,80,d9,87,d,64
  //   ,d6,21,17,20,c,a,15,5e,46,3a,91,f0,78,93,7a,86,69,8e,8b,55,f4,13
endmodule
