// Digital circuit หุ่นยนรีบๆเดินดิวะ.dig as structural Verilog
module \ห__นยนร_บๆเด_นด_วะ  (
  input  [7:0] A,
  input  reset,
  input  clk,
  output out_3,
  output out_4
);

  wire Add_out, and_1_out, and_2_out, and_3_out, and_4_out, clk_t, comparator_2_eq, comparator_3_eq,
       d_ff_2_q, d_ff_3_q, d_ff_4_q, d_ff_8_nq, d_ff_8_q, d_ff_9_nq, d_ff_9_q, d_ff_10_nq, d_ff_10_q,
       d_ff_11_nq, d_ff_11_q, d_ff_12_nq, d_ff_12_q, d_ff_13_nq, d_ff_13_q, d_ff_14_q, d_ff_15_q, d_ff_16_q,
       d_ff_17_q, d_ff_18_nq, delay_1_out, delay_2_out, delay_3_out, multiplexer_3_out, not_1_out, not_2_out,
       or_1_out, start_out, xnor_1_out, xnor_2_out, xnor_3_out, xnor_4_out, xnor_5_out, xnor_6_out, \เขว ,
       \เหล_อง , \แดง ;
  wire [1:0] Z;
  wire [11:0] add_2_s, d_ff_1_q, d_ff_5_q, div_1_q, div_1_r, multiplexer_1_out, multiplexer_2_out;

  Button start (.out(start_out));
  and and_1 (and_1_out, \เขว , start_out);
  and and_2 (and_2_out, start_out, \เหล_อง );
  and and_3 (and_3_out, start_out, \แดง );
  Button Add (.out(Add_out));
  not not_1 (not_1_out, Z[1]);
  D_FF #(.Bits(12)) d_ff_1 (.D(multiplexer_1_out), .C(Add_out), .Q(d_ff_1_q));  // open: nQ
  not not_2 (not_2_out, Z[0]);
  and and_4 (and_4_out, not_2_out, not_1_out);
  D_FF d_ff_2 (.D(and_1_out), .C(delay_1_out), .Q(d_ff_2_q));  // open: nQ
  Delay delay_1 (.in(start_out), .out(delay_1_out));
  D_FF d_ff_3 (.D(and_2_out), .C(delay_2_out), .Q(d_ff_3_q));  // open: nQ
  Delay delay_2 (.in(start_out), .out(delay_2_out));
  D_FF d_ff_4 (.D(and_3_out), .C(delay_3_out), .Q(d_ff_4_q));  // open: nQ
  Delay delay_3 (.in(start_out), .out(delay_3_out));
  D_FF #(.Bits(12)) d_ff_5 (.D({4'b0000, A}), .C(Add_out), .Q(d_ff_5_q));  // open: nQ
  xnor xnor_1 (xnor_1_out, d_ff_2_q, d_ff_8_nq);
  xnor xnor_2 (xnor_2_out, d_ff_3_q, d_ff_9_nq);
  xnor xnor_3 (xnor_3_out, d_ff_4_q, d_ff_10_nq);
  Multiplexer #(.Bits(12)) multiplexer_1 (.sel(reset), .in_0(add_2_s), .in_1({12{1'b0}}), .out(multiplexer_1_out));
  Multiplexer #(.Bits(12)) multiplexer_2 (.sel(reset), .in_0(d_ff_5_q), .in_1({12{1'b0}}), .out(multiplexer_2_out));
  Button button_1 (.out(clk_t));
  D_FF d_ff_6 (.D(Z[0]), .C(clk_t), .Q(Z[1]));  // open: nQ
  D_FF d_ff_7 (.D(and_4_out), .C(clk_t), .Q(Z[0]));  // open: nQ
  D_FF d_ff_8 (.D(xnor_1_out), .C(clk_t), .Q(d_ff_8_q), .nQ(d_ff_8_nq));
  D_FF d_ff_9 (.D(xnor_2_out), .C(clk_t), .Q(d_ff_9_q), .nQ(d_ff_9_nq));
  D_FF d_ff_10 (.D(xnor_3_out), .C(clk_t), .Q(d_ff_10_q), .nQ(d_ff_10_nq));
  Add #(.Bits(12)) add_2 (.a(d_ff_1_q), .b(multiplexer_2_out), .c_i(1'b0), .s(add_2_s));  // open: c_o
  xnor xnor_4 (xnor_4_out, d_ff_8_q, d_ff_11_nq);
  xnor xnor_5 (xnor_5_out, d_ff_9_q, d_ff_12_nq);
  Comparator #(.Bits(2)) comparator_1 (.a(2'b01), .b(Z), .gt(\เขว ), .eq(\เหล_อง ), .lt(\แดง ));
  Div #(.Bits(12)) div_1 (.a(add_2_s), .b(12'h3), .q(div_1_q), .r(div_1_r));
  D_FF d_ff_11 (.D(xnor_4_out), .C(clk_t), .Q(d_ff_11_q), .nQ(d_ff_11_nq));
  D_FF d_ff_12 (.D(xnor_5_out), .C(clk_t), .Q(d_ff_12_q), .nQ(d_ff_12_nq));
  Comparator #(.Bits(12)) comparator_2 (.a({12{1'b0}}), .b(div_1_q), .eq(comparator_2_eq));  // open: gt, lt
  Comparator #(.Bits(12)) comparator_3 (.a(div_1_r), .b({12{1'b0}}), .eq(comparator_3_eq));  // open: gt, lt
  LED led_1 (.in(\เขว ));
  xnor xnor_6 (xnor_6_out, d_ff_11_q, d_ff_13_nq);
  and and_5 (out_3, ~comparator_2_eq, multiplexer_3_out);  // And
  Multiplexer multiplexer_3 (.sel(comparator_3_eq), .in_0(1'b0), .in_1(1'b1), .out(multiplexer_3_out));
  LED led_2 (.in(\เหล_อง ));
  D_FF d_ff_13 (.D(xnor_6_out), .C(clk_t), .Q(d_ff_13_q), .nQ(d_ff_13_nq));
  LED led_3 (.in(\แดง ));
  or or_1 (or_1_out, d_ff_13_q, d_ff_12_q, d_ff_10_q);
  D_FF d_ff_14 (.D(or_1_out), .C(clk), .Q(d_ff_14_q));  // open: nQ
  D_FF d_ff_15 (.D(d_ff_14_q), .C(clk), .Q(d_ff_15_q));  // open: nQ
  D_FF d_ff_16 (.D(d_ff_15_q), .C(clk), .Q(d_ff_16_q));  // open: nQ
  D_FF d_ff_17 (.D(d_ff_16_q), .C(clk), .Q(d_ff_17_q));  // open: nQ
  D_FF d_ff_18 (.D(d_ff_17_q), .C(clk), .nQ(d_ff_18_nq));  // open: Q
  and and_6 (out_4, d_ff_18_nq, or_1_out);

  // Other names for the same wires on the sheet: res = reset
endmodule
