// Digital circuit ไฟข้ามถนน.dig as structural Verilog
module \ไฟข_ามถนน  (
  input  clk,
  input  clk_2,
  input  clk_3
);

  wire _1, _2, _3, and_1_out, comparator_1_eq, comparator_2_eq, comparator_3_eq, comparator_4_eq,
       comparator_5_eq, comparator_6_eq, comparator_7_eq, comparator_8_eq, comparator_9_eq, comparator_10_eq,
       d_ff_3_q, d_ff_4_q, d_ff_5_q, d_ff_6_q, d_ff_7_nq, d_ff_7_q, d_ff_8_nq, d_ff_8_q, or_1_out, or_2_out,
       or_3_out, or_4_out, or_5_out, or_6_out, or_7_out, or_8_out, or_9_out, s1, s2, s3, s4, t_ff_1_q, \คข1 ,
       \คด1 , \คด3 , \คห1 ;
  wire [2:0] z1, z2;

  D_FF #(.Bits(3)) d_ff_1 (.D({_3, _2, _1}), .C(or_1_out), .Q(z1));  // open: nQ
  or or_1 (or_1_out, _1, _2, _3);
  Comparator #(.Bits(3)) comparator_1 (.a(z1), .b(3'b100), .eq(comparator_1_eq));  // open: gt, lt
  Comparator #(.Bits(3)) comparator_2 (.a(z1), .b(3'b000), .eq(comparator_2_eq));  // open: gt, lt
  or or_2 (or_2_out, comparator_1_eq, comparator_2_eq);
  T_FF t_ff_1 (.T(1'b1), .C(clk), .Q(t_ff_1_q));  // open: nQ
  D_FF #(.Bits(3)) d_ff_2 (.D(z1), .C(or_3_out), .Q(z2));  // open: nQ
  or or_3 (or_3_out, _1, _2, _3);
  and and_1 (and_1_out, or_2_out, t_ff_1_q);
  Button \u_รถผ_าน  (.out(_1));
  Button \u_คนข_าม  (.out(_2));
  Button \u_ระว_ง  (.out(_3));
  Comparator #(.Bits(3)) comparator_3 (.a(z2), .b(3'b010), .eq(comparator_3_eq));  // open: gt, lt
  Comparator #(.Bits(3)) comparator_4 (.a(z1), .b(3'b001), .eq(comparator_4_eq));  // open: gt, lt
  Comparator #(.Bits(3)) comparator_5 (.a(z2), .b(3'b010), .eq(comparator_5_eq));  // open: gt, lt
  Comparator #(.Bits(3)) comparator_6 (.a(z1), .b(3'b001), .eq(comparator_6_eq));  // open: gt, lt
  or or_4 (or_4_out, \คห1 , and_1_out);
  or or_5 (or_5_out, \คด3 , and_1_out);
  LED \u_คน  (.in(or_4_out));
  LED \u_รถ  (.in(or_5_out));
  and and_2 (s1, comparator_3_eq, comparator_4_eq);
  and and_3 (s3, ~comparator_5_eq, comparator_6_eq);  // And
  or or_6 (or_6_out, \คข1 , s4);
  or or_7 (or_7_out, \คด1 , s3);
  LED \u_คน_2  (.in(or_6_out));
  D_FF d_ff_3 (.D(s1), .C(clk_2), .Q(d_ff_3_q));  // open: nQ
  D_FF d_ff_4 (.D(s2), .C(clk_3), .Q(d_ff_4_q));  // open: nQ
  LED \u_รถ_2  (.in(or_7_out));
  D_FF d_ff_5 (.D(d_ff_3_q), .C(clk_2), .Q(d_ff_5_q));  // open: nQ
  D_FF d_ff_6 (.D(d_ff_4_q), .C(clk_3), .Q(d_ff_6_q));  // open: nQ
  Comparator #(.Bits(3)) comparator_7 (.a(z2), .b(3'b001), .eq(comparator_7_eq));  // open: gt, lt
  Comparator #(.Bits(3)) comparator_8 (.a(z1), .b(3'b010), .eq(comparator_8_eq));  // open: gt, lt
  Comparator #(.Bits(3)) comparator_9 (.a(z2), .b(3'b001), .eq(comparator_9_eq));  // open: gt, lt
  Comparator #(.Bits(3)) comparator_10 (.a(z1), .b(3'b010), .eq(comparator_10_eq));  // open: gt, lt
  or or_8 (or_8_out, \คด1 , \คด3 , s3);
  D_FF d_ff_7 (.D(d_ff_5_q), .C(clk_2), .Q(d_ff_7_q), .nQ(d_ff_7_nq));
  D_FF d_ff_8 (.D(d_ff_6_q), .C(clk_3), .Q(d_ff_8_q), .nQ(d_ff_8_nq));
  or or_9 (or_9_out, \คข1 , \คห1 , s4);
  and and_4 (s2, comparator_7_eq, comparator_8_eq);
  and and_5 (s4, ~comparator_9_eq, comparator_10_eq);  // And
  LED \u_คน_3  (.in(or_8_out));
  and and_6 (\คด1 , s1, d_ff_7_q);
  and and_7 (\คห1 , d_ff_7_nq, s1);
  and and_8 (\คข1 , s2, d_ff_8_q);
  and and_9 (\คด3 , d_ff_8_nq, s2);
  LED \u_รถ_3  (.in(or_9_out));

  // Other names for the same wires on the sheet: รข1 = \คด1 ; คด2 = s3; รข2 = s3; รด1 = \คข1 ; คข2 = s4; รด2 = s4;
  //   รด3 = \คห1 ; รห1 = \คด3 

  // Notes on the sheet:
  //   clk: Hz: 2
endmodule
